# Fritzing sketch modèle_électronique_arduino (saved by Fritzing 0.9.3b)
breadboards: 1

parts:
  Composant1 = Arduino Uno (Rev3)
  R1 = Resistor [tolerance=±5% resistance=1k package=THT]
  D1 = LTE-302 [package=lte-302]
  U1 = LM124-324 Quad Opamp [package="DIP (Dual Inline)"]
  R2 = Resistor [tolerance=±5% resistance=68k package="1206 [SMD]"]
  C1 = Ceramic Capacitor [capacitance=1µF package="0805 [SMD, multilayer]"]
  R3 = Resistor [tolerance=±5% resistance=10k package="2010 [SMD]"]
  Q1 = LTR-301 [package=ltr-301]
  C2 = Ceramic Capacitor [capacitance=1µF package="0805 [SMD, multilayer]"]
  R4 = Resistor [tolerance=±5% resistance=8.2k package="1206 [SMD]"]
  C3 = Ceramic Capacitor [capacitance="100 nF" package="0805 [SMD, multilayer]"]
  C4 = Ceramic Capacitor [capacitance="100 nF" package="0805 [SMD, multilayer]"]
  R5 = Resistor [tolerance=±5% resistance=1k package="1206 [SMD]"]
  R6 = Resistor [tolerance=±5% resistance=470k package="1206 [SMD]"]
  R7 = Resistor [tolerance=±5% resistance=1.8k package="1206 [SMD]"]
  Q2 = NPN-Transistor [package="SOT-23 [SMD]"]
  R8 = Resistor [tolerance=±5% resistance=68k package=THT]

nets:
  N1: Composant1.A0, R7.Pin_1, Q2.0
  N2: Composant1.5V, R1.Pin_1, R3.Pin_1, Q2.2
  N3: Composant1.GND, D1.A, U1.VCC-, R2.Pin_1, C1.1, Q1.E, R4.Pin_0, R5.Pin_1, R8.Pin_0
  N4: R1.Pin_0, D1.C, U1.1IN+, U1.VCC+, R2.Pin_0
  N5: U1.1OUT, C2.1, C3.1
  N6: U1.1IN-, C3.0, R8.Pin_1
  N7: U1.4IN+, C2.0, R4.Pin_1
  N8: U1.4IN-, R6.Pin_0
  N9: U1.4OUT, C4.1, R7.Pin_0
  N10: C1.0, R3.Pin_0, Q1.C
  N11: C4.0, R5.Pin_0, R6.Pin_1
